# Fritzing sketch i2c master (saved by Fritzing 0.9.3b)
circuit board: 2.31118cm x 4.27655cm
breadboards: 1

parts:
  Composant1 = Arduino Pro Micro (Clone)
  J1 = female pin header, 4 pins [form="♀ (female)"]

nets:
  N1: Composant1.GND, J1.pin4
  N2: Composant1.D2, J1.pin1
  N3: Composant1.D3, J1.pin2
  N4: Composant1.VCC, J1.pin3
