# Fritzing sketch sensors (saved by Fritzing 0.9.3b)
circuit board: 6.73642cm x 6.7982cm
breadboards: 1

parts:
  Composant1 = Arduino Nano (Rev3.0) (ICSP)
  I2C = female pin header, 4 pins [form="♀ (female)"]
  MOVING = female pin header, 5 pins [form="♀ (female)"]
  HEAT = female pin header, 3 pins [form="♀ (female)"]
  TRIM = female pin header, 3 pins [form="♀ (female)"]
  POWER = female pin header, 5 pins [form="♀ (female)"]
  INTER_XM = female pin header, 5 pins [form="♀ (female)"]
  INTER_XL = female pin header, 4 pins [form="♀ (female)"]

nets:
  GND: Composant1.GND, I2C.pin4, MOVING.pin5, HEAT.pin3, TRIM.pin3, POWER.pin5, INTER_XM.pin5, INTER_XL.pin4
  N1: Composant1.D2, MOVING.pin3
  N2: Composant1.D3, INTER_XM.pin4
  N3: Composant1.D4, INTER_XM.pin3
  N4: Composant1.D5, INTER_XL.pin3
  N5: Composant1.D6, INTER_XL.pin2
  N6: Composant1.D7, INTER_XM.pin2
  N7: Composant1.D8, INTER_XM.pin1
  N8: Composant1.D9, INTER_XL.pin1
  N9: Composant1.D10, MOVING.pin2
  5V: Composant1.VIN, I2C.pin3, MOVING.pin4, HEAT.pin2, TRIM.pin2, POWER.pin4
  Roll: Composant1.A7, MOVING.pin1
  Trim: Composant1.A6, TRIM.pin1
  SCL: Composant1.A5, I2C.pin2
  SDA: Composant1.A4, I2C.pin1
  Mix: Composant1.A3, POWER.pin1
  Prop: Composant1.A2, POWER.pin2
  Throttle: Composant1.A1, POWER.pin3
  Heat: Composant1.A0, HEAT.pin1
